# Fritzing sketch リニアモーターカー (saved by Fritzing 0.9.5d)
breadboards: 2

parts:
  パーツ1 = Arduino Nano (Rev3.0)
  R1 = Rotary Potentiometer (Small) [maximum_resistance=100kΩ package=THT]
  M1 = DC Motor
  S1 = SPST Switch [package=switche-dpdt]
  VCC1 = Battery
  U3 = TA7291P [package=HSIP10-P-2.54(THT)]
  D1 = LED_BARGRAPH_10 [package=led_bargaph_10]

nets:
  GND: パーツ1.GND, R1.leg2, S1.S, VCC1.-, U3.GND, D1.A_A, D1.B_A, D1.C_A, D1.D_A, D1.E_A, D1.F_A, D1.G_A, D1.H_A, D1.I_A, D1.J_A
  N1: パーツ1.D3, S1.O
  N2: パーツ1.D5, U3.Vref
  N3: パーツ1.D6, U3.IN1
  N4: パーツ1.D7, U3.IN2
  N5: パーツ1.D8, D1.J_C, D1.I_C
  N6: パーツ1.D9, D1.H_C, D1.G_C
  N7: パーツ1.D10, D1.F_C, D1.E_C
  N8: パーツ1.D11/MOSI, D1.D_C, D1.C_C
  N9: パーツ1.D12/MISO, D1.B_C, D1.A_C
  5V: パーツ1.5V, R1.leg1, U3.Vcc
  N10: パーツ1.A0, R1.wiper
  N11: M1.pin_1, U3.OUT2
  N12: M1.pin_2, U3.OUT1
  net label: VCC1.+, U3.Vs

custom parts:
  TA7291P: The IC are Full-Bridge Driver. 4 modes available (CW / CCW / STOP / BRAKE) and PWM control. Output current:1.0 A (AVE.) 2.0 A (PEAK)
